// Digital circuit Inc-class-participation(PC) .dig as structural Verilog
module Inc_class_participation_PC (
  input  [1:0] CSL,
  input  [3:0] Input,
  input  Clock,
  input  [3:0] Inc,
  output [3:0] Output
);

  wire [3:0] add_1_s, multiplexer_1_out;

  Add #(.Bits(4)) add_1 (.a(Output), .b(Inc), .c_i(1'b0), .s(add_1_s));  // open: c_o
  Multiplexer #(.Selector_Bits(2), .Bits(4)) multiplexer_1 (
    .sel(CSL), .in_0(4'b0000), .in_1(Input), .in_2(Output), .in_3(add_1_s), .out(multiplexer_1_out));
  D_FF D_3 (.D(multiplexer_1_out[3]), .C(Clock), .Q(Output[3]));  // open: nQ
  D_FF D_2 (.D(multiplexer_1_out[2]), .C(Clock), .Q(Output[2]));  // open: nQ
  D_FF D_1 (.D(multiplexer_1_out[1]), .C(Clock), .Q(Output[1]));  // open: nQ
  D_FF D_0 (.D(multiplexer_1_out[0]), .C(Clock), .Q(Output[0]));  // open: nQ

  // Notes on the sheet:
  //   CSL: 0 = Clear
  //   1 = Store Input
  //   2 = Load
  //   3 = Set all bits equal to 1 (F)
  //   Input: Clear/Store/Load
endmodule
