// Digital circuit register_files.dig as structural Verilog
module register_files (
  input  [7:0] Control_signals,
  input  clk,
  input  [1:0] RR_1,
  input  [1:0] RR_2,
  input  [1:0] WR,
  input  [3:0] Write_data,
  output [3:0] ReadData1,
  output [3:0] ReadData2
);

  wire [3:0] demultiplexer_1_out_0, demultiplexer_1_out_1, demultiplexer_1_out_2, demultiplexer_1_out_3,
       R_0_p4, R_1_p4, R_2_p4, R_3_p4;

  Demultiplexer #(.Selector_Bits(2), .Bits(4)) demultiplexer_1 (
    .sel(WR), .in(Write_data), .out_0(demultiplexer_1_out_0), .out_1(demultiplexer_1_out_1),
    .out_2(demultiplexer_1_out_2), .out_3(demultiplexer_1_out_3));
  // GPR R_0: pin names not known; wires that end beside it: Control_signals[1:0], demultiplexer_1_out_0, clk, R_0_p4
  // GPR R_1: pin names not known; wires that end beside it: Control_signals[3:2], demultiplexer_1_out_1, clk, R_1_p4
  // GPR R_2: pin names not known; wires that end beside it: Control_signals[5:4], demultiplexer_1_out_2, clk, R_2_p4
  // GPR R_3: pin names not known; wires that end beside it: Control_signals[7:6], demultiplexer_1_out_3, clk, R_3_p4
  Multiplexer #(.Selector_Bits(2), .Bits(4)) multiplexer_1 (
    .sel(RR_1), .in_0(R_0_p4), .in_1(R_1_p4), .in_2(R_2_p4), .in_3(R_3_p4), .out(ReadData1));
  Multiplexer #(.Selector_Bits(2), .Bits(4)) multiplexer_2 (
    .sel(RR_2), .in_0(R_0_p4), .in_1(R_1_p4), .in_2(R_2_p4), .in_3(R_3_p4), .out(ReadData2));
endmodule
